# Fritzing sketch Rayomatic_2026 v1.5 (saved by Fritzing 0.9.3b)
circuit board: 10cm x 10cm

parts:
  SCL_SDA_5V_GND = female pin header, 4 pins [form="♀ (female)"]
  ZS-042_RTC3 = ZS-042 RTC Module
  C2 = Electrolytic Capacitor [capacitance=1µF package="100 mil [THT, electrolytic]"]
  Reader2 = female pin header, 8 pins [form="♀ (female)"]
  Buzzer = female pin header, 2 pins [form="♀ (female)"]
  I2C3 = female pin header, 4 pins [form="♀ (female)"]
  J12 = female pin header, 15 pins [form="♀ (female)"]
  J13 = female pin header, 15 pins [form="♀ (female)"]
  J14 = female pin header, 15 pins [form="♀ (female)"]
  J15 = female pin header, 15 pins [form="♀ (female)"]
  Power_plug1 = Power plug
  Wippe = female pin header, 3 pins [form="♀ (female)"]
  Anzeige = female pin header, 3 pins [form="♀ (female)"]
  C3 = Electrolytic Capacitor [capacitance=1µF package="100 mil [THT, electrolytic]"]
  J18 = female pin header, 6 pins [form="♀ (female)"]

nets:
  N1: SCL_SDA_5V_GND.pin1, ZS-042_RTC3.SCL, I2C3.pin4
  N2: SCL_SDA_5V_GND.pin2, ZS-042_RTC3.SDA, I2C3.pin3
  N3: SCL_SDA_5V_GND.pin3, ZS-042_RTC3.VCC, C2.+, I2C3.pin2, J18.pin1
  N4: SCL_SDA_5V_GND.pin4, ZS-042_RTC3.GND#6, C2.-, Buzzer.pin1, I2C3.pin1, J18.pin6
  N5: Reader2.pin6, Power_plug1.GND, Wippe.pin1, Anzeige.pin1, C3.-
  N6: J12.pin1, J13.pin1
  N7: J12.pin2, J13.pin2
  N8: J12.pin3, J13.pin3
  N9: J12.pin4, J13.pin4
  N10: J12.pin5, J13.pin5
  N11: J12.pin6, J13.pin6
  N12: J12.pin7, J13.pin7
  N13: J12.pin8, J13.pin8
  N14: J12.pin9, J13.pin9
  N15: J12.pin10, J13.pin10
  N16: J12.pin11, J13.pin11
  N17: J12.pin12, J13.pin12
  N18: J12.pin13, J13.pin13
  N19: J12.pin14, J13.pin14
  N20: J12.pin15, J13.pin15
  N21: J14.pin1, J15.pin1
  N22: J14.pin2, J15.pin2
  N23: J14.pin3, J15.pin3
  N24: J14.pin4, J15.pin4
  N25: J14.pin5, J15.pin5
  N26: J14.pin6, J15.pin6
  N27: J14.pin7, J15.pin7
  N28: J14.pin8, J15.pin8
  N29: J14.pin9, J15.pin9
  N30: J14.pin10, J15.pin10
  N31: J14.pin11, J15.pin11
  N32: J14.pin12, J15.pin12
  N33: J14.pin13, J15.pin13
  N34: J14.pin14, J15.pin14
  N35: J14.pin15, J15.pin15
  N36: Power_plug1.VCC, Wippe.pin2, Anzeige.pin2, C3.+

notes:
  Servo Wippe 13
  CS D31
  RST D7
  SDA D22
  CS MOSI MISO CLK GND 3,3 VIN
  SDA SCK MOSI MISO - GND RST 3,3
  GND VCC SDA SCL
  Buzzer D6
  Servo Anzeige 11
