# Fritzing sketch Rayomatic_2026 v2.0 (saved by Fritzing 0.9.3b)
circuit board: 10cm x 10.5cm

parts:
  M1 = Mega2560 R3 Pro ch340g
  SCL_SDA_5V_GND = female pin header, 4 pins [form="♀ (female)"]
  ZS-042_RTC3 = ZS-042 RTC Module
  C2 = Electrolytic Capacitor [capacitance=1µF package="100 mil [THT, electrolytic]"]
  Bauteil5 = TXB0108 8-channel Bi-directional Logic Level Converter
  Reader2 = female pin header, 8 pins [form="♀ (female)"]
  Buzzer = female pin header, 2 pins [form="♀ (female)"]
  I2C3 = female pin header, 4 pins [form="♀ (female)"]
  Bauteil6 = Adafruit SPI Flash SD Card [part_number="Adafruit #4899"]
  Power_plug1 = Power plug
  Wippe = female pin header, 3 pins [form="♀ (female)"]
  Anzeige = female pin header, 3 pins [form="♀ (female)"]
  C3 = Electrolytic Capacitor [capacitance=1µF package="100 mil [THT, electrolytic]"]
  GND_42_40_38_36_+ = female pin header, 6 pins [form="♀ (female)"]
  J16 = female pin header, 15 pins [form="♀ (female)"]
  J17 = female pin header, 15 pins [form="♀ (female)"]
  J18 = female pin header, 15 pins [form="♀ (female)"]
  J19 = female pin header, 15 pins [form="♀ (female)"]
  J20 = female pin header, 15 pins [form="♀ (female)"]
  J21 = female pin header, 15 pins [form="♀ (female)"]
  RX2-TX = female pin header, 2 pins [form="♀ (female)"]
  TX2-RX = female pin header, 2 pins [form="♀ (female)"]
  Pixel_1 = female pin header, 3 pins [form="♀ (female)"]
  Pixel_2 = female pin header, 3 pins [form="♀ (female)"]
  LED_1 = female pin header, 2 pins [form="♀ (female)"]
  LED_2 = female pin header, 2 pins [form="♀ (female)"]

nets:
  N1: M1.A3, LED_2.pin1
  N2: M1.A5, LED_1.pin1
  N3: M1.42, GND_42_40_38_36_+.pin5
  N4: M1.40, GND_42_40_38_36_+.pin4
  N5: M1.38, GND_42_40_38_36_+.pin3
  N6: M1.36, GND_42_40_38_36_+.pin2
  N7: M1.A14, Pixel_2.pin1
  N8: M1.A2, Pixel_1.pin1
  N9: M1.7▀, Reader2.pin7
  N10: M1.11▀, Anzeige.pin3
  N11: M1.13▀, Wippe.pin3
  N12: M1.17, RX2-TX.pin2
  N13: M1.21, SCL_SDA_5V_GND.pin1, ZS-042_RTC3.SCL, I2C3.pin4
  N14: M1.31, Bauteil5.B4
  N15: M1.22, Bauteil5.B8
  N16: M1.20, SCL_SDA_5V_GND.pin2, ZS-042_RTC3.SDA, I2C3.pin3
  N17: M1.16, TX2-RX.pin2
  N18: M1.6▀, Buzzer.pin2
  GND: M1.GND-1, M1.GND-2, M1.GND-3, SCL_SDA_5V_GND.pin4, ZS-042_RTC3.GND#6, C2.-, Bauteil5.GND, Reader2.pin6, Buzzer.pin1, I2C3.pin1, Bauteil6.GND, Power_plug1.GND, Wippe.pin1, Anzeige.pin1, C3.-, GND_42_40_38_36_+.pin6, J18.pin14, J19.pin14, J21.pin14, Pixel_1.pin3, Pixel_2.pin3, LED_1.pin2, LED_2.pin2
  N19: M1.RST-1, J18.pin7, J19.pin7, J21.pin7
  N20: M1.3V3-2, Bauteil5.OE, Bauteil5.VCCA, Reader2.pin8, Bauteil6.VIN
  N21: M1.51/MOSI-1, M1.51/MOSI-2, Bauteil5.B6
  N22: M1.52/SCK-1, Bauteil5.B7
  N23: M1.50/MISO-1, Bauteil5.B5
  N24: M1.VTG, M1.5V-1, M1.5V-2, SCL_SDA_5V_GND.pin3, ZS-042_RTC3.VCC, C2.+, Bauteil5.VCCB, I2C3.pin2, GND_42_40_38_36_+.pin1
  N25: Bauteil5.A8, Reader2.pin1
  N26: Bauteil5.A7, Reader2.pin2, Bauteil6.SCK
  N27: Bauteil5.A6, Reader2.pin3, Bauteil6.MOSI
  N28: Bauteil5.A5, Reader2.pin4, Bauteil6.MISO_3.3V
  N29: Bauteil5.A4, Bauteil6.SS
  N30: Power_plug1.VCC, Wippe.pin2, Anzeige.pin2, C3.+
  N31: J16.pin1, J17.pin1, J20.pin1
  N32: J16.pin2, J17.pin2, J20.pin2
  N33: J16.pin3, J17.pin3, J20.pin3
  N34: J16.pin4, J17.pin4, J20.pin4
  N35: J16.pin5, J17.pin5, J20.pin5
  N36: J16.pin6, J17.pin6, J20.pin6
  N37: J16.pin7, J17.pin7, J20.pin7
  N38: J16.pin8, J17.pin8, J20.pin8
  N39: J16.pin9, J17.pin9, J20.pin9
  N40: J16.pin10, J17.pin10, J20.pin10
  N41: J16.pin11, J17.pin11, J20.pin11
  N42: J16.pin12, J17.pin12, J20.pin12
  N43: J16.pin13, J17.pin13, J20.pin13
  N44: J16.pin14, J17.pin14, J20.pin14, TX2-RX.pin1
  N45: J16.pin15, J17.pin15, J20.pin15, RX2-TX.pin1
  N46: J18.pin1, J19.pin1, J21.pin1
  N47: J18.pin2, J19.pin2, J21.pin2
  N48: J18.pin3, J19.pin3, J21.pin3
  N49: J18.pin4, J19.pin4, J21.pin4
  N50: J18.pin5, J19.pin5, J21.pin5
  N51: J18.pin6, J19.pin6, J21.pin6
  N52: J18.pin8, J19.pin8, J21.pin8
  N53: J18.pin9, J19.pin9, J21.pin9
  N54: J18.pin10, J19.pin10, J21.pin10
  N55: J18.pin11, J19.pin11, J21.pin11
  N56: J18.pin12, J19.pin12, J21.pin12
  N57: J18.pin13, J19.pin13, J21.pin13
  N58: J18.pin15, J19.pin15, J21.pin15
  N59: Pixel_1.pin2, Pixel_2.pin2

notes:
  Buzzer D6
  CS D31
  RST D7
  SDA D22
  CS MOSI MISO CLK GND 3,3 VIN
  SDA SCK MOSI MISO - GND RST 3,3
  GND VCC SDA SCL
  Wippe D13
  Anzeige D11
  Pixel1 A2
  Pixel2 A14
  LED 1 A5
  LED 2 A3

custom parts:
  Mega2560 R3 Pro ch340g: The Mega 2560 R3 Pro Mini :- Completely compatible with original Arduino Mega2560 Pin pitch: 0.1 inch Size: 5.42cm*3.68cm With Atmega16U2 chip as the USB to Serial converter 5V working voltage. Input Voltage:7-12V Analog Input Pins: 16 Digital I/O pins: 54 The Mega 2560 R3 Pro Mini has no datasheet and no info and I don't have one to compare, so I made this based on photos. Dec 2019 modified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
  TXB0108 8-channel Bi-directional Logic Level Converter: Because the Arduino (and Basic Stamp) are 5V devices, and most modern sensors, displays, flash cards and modes are 3.3V-only, many makers find that they need to perform level shifting/conversion to protect the 3.3V device from 5V. Although one can use resistors to make a divider, for high speed transfers, the resistors can add a lot of slew and cause havoc that is tough to debug. For that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
  Adafruit SPI Flash SD Card: This breakout is for a fascinating chip - it looks like an SPI Flash storage chip (like the GD25Q16) but its really an SD card, in an SMT chip format. What that means is that you wire up like an SD card breakout, and use the SD card libraries you already have for your microcontroller. For example, you can use the built in SD library in Arduino, or for CircuitPython we have an sdcard library.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
