# Fritzing sketch Geigerzähler 2022 V.3_Master (saved by Fritzing 0.9.3b)
circuit board: 6cm x 4cm
breadboards: 1

parts:
  D3_GND = female pin header, 2 pins [form="♀ (female)"]
  GND_A3_VCC = female pin header, 3 pins [form="♀ (female)"]
  GND_A2 = female pin header, 2 pins [form="♀ (female)"]
  GND_VCC_SDA_SCL = female pin header, 4 pins [form="♀ (female)"]
  Vcc_GND_SDA_SCL = female pin header, 6 pins [form="♀ (female)"]
  SDA_SCK_MOSI_MISO_GND_RST_3_3V = female pin header, 8 pins [form="♀ (female)"]
  Nano = Arduino Nano (Rev3.0)
  GND_VIN_>5V = Battery block 9V
  SW1 = DIP Switch 4 Position [package=dipswitch-04]
  Gnd_Vin_5V = female pin header, 2 pins [form="♀ (female)"]
  Switch = female pin header, 2 pins [form="♀ (female)"]
  Switch_2 = female pin header, 2 pins [form="♀ (female)"]
  A7_A6_A1_A0 = double row female pin header, 8 pins [form="♀ (female)"]

nets:
  N1: D3_GND.pin1, Nano.D3
  N2: D3_GND.pin2, GND_A3_VCC.pin1, GND_A2.pin1, GND_VCC_SDA_SCL.pin1, Vcc_GND_SDA_SCL.pin2, SDA_SCK_MOSI_MISO_GND_RST_3_3V.pin6, Nano.GND, GND_VIN_>5V.-, SW1.5, SW1.6, SW1.7, SW1.8, Gnd_Vin_5V.pin2, A7_A6_A1_A0.pin1, A7_A6_A1_A0.pin2, A7_A6_A1_A0.pin3, A7_A6_A1_A0.pin4
  N3: GND_A3_VCC.pin2, Nano.A3
  N4: GND_A3_VCC.pin3, GND_VCC_SDA_SCL.pin2, Vcc_GND_SDA_SCL.pin1, Nano.5V, Switch_2.pin2
  N5: GND_A2.pin2, Nano.A2
  N6: GND_VCC_SDA_SCL.pin3, Vcc_GND_SDA_SCL.pin3, Nano.A4
  N7: GND_VCC_SDA_SCL.pin4, Vcc_GND_SDA_SCL.pin4, Nano.A5
  N8: SDA_SCK_MOSI_MISO_GND_RST_3_3V.pin1, Nano.D10
  N9: SDA_SCK_MOSI_MISO_GND_RST_3_3V.pin2, Nano.D13/SCK
  N10: SDA_SCK_MOSI_MISO_GND_RST_3_3V.pin3, Nano.D11/MOSI
  N11: SDA_SCK_MOSI_MISO_GND_RST_3_3V.pin4, Nano.D12/MISO
  N12: SDA_SCK_MOSI_MISO_GND_RST_3_3V.pin7, Nano.D9
  N13: SDA_SCK_MOSI_MISO_GND_RST_3_3V.pin8, Nano.3V3
  N14: Nano.D4, SW1.1
  N15: Nano.D5, SW1.2
  N16: Nano.D7, SW1.3
  N17: Nano.D8, SW1.4
  N18: Nano.VIN, Switch.pin1
  N19: Nano.A7, A7_A6_A1_A0.pin8
  N20: Nano.A6, A7_A6_A1_A0.pin7
  N21: Nano.A1, A7_A6_A1_A0.pin6
  N22: Nano.A0, A7_A6_A1_A0.pin5
  N23: GND_VIN_>5V.+, Switch.pin2
  N24: Gnd_Vin_5V.pin1, Switch_2.pin1

notes:
  Poti A3
  Analog D3
  Buzzer A2
  SDA
  SCK
  MOSI
  MISO
  RST
  VIN
  Geigerzaehler 2022 V3
  Platine Vin
  Gnd
  Buzzer
  Analog
  LCD
  Poti
  Blau/ Gelb
  2/4 Reihen
  Free 1
  Free 2
