# Fritzing sketch Geigerzähler 2023 V.4_Master (saved by Fritzing 0.9.3b)
circuit board: 6cm x 4cm
breadboards: 1

parts:
  D3_GND = female pin header, 2 pins [form="♀ (female)"]
  GND_A3_VCC = female pin header, 3 pins [form="♀ (female)"]
  GND_A2 = female pin header, 2 pins [form="♀ (female)"]
  GND_VCC_SDA_SCL = female pin header, 4 pins [form="♀ (female)"]
  Vcc_GND_SDA_SCL = female pin header, 6 pins [form="♀ (female)"]
  SDA_SCK_MOSI_MISO_GND_RST_3_3V = female pin header, 8 pins [form="♀ (female)"]
  Nano = Arduino Nano (Rev3.0)
  GND_VIN_>5V = Battery block 9V
  Switch = female pin header, 2 pins [form="♀ (female)"]
  GND_VCC_SDA_SCL1 = female pin header, 4 pins [form="♀ (female)"]
  GND_A7_VCC = female pin header, 3 pins [form="♀ (female)"]
  RGB = female pin header, 4 pins [form="♀ (female)"]  # not connected

nets:
  N1: D3_GND.pin1, Nano.D3
  N2: D3_GND.pin2, GND_A3_VCC.pin1, GND_A2.pin1, GND_VCC_SDA_SCL.pin1, Vcc_GND_SDA_SCL.pin2, SDA_SCK_MOSI_MISO_GND_RST_3_3V.pin6, Nano.GND, GND_VIN_>5V.-, GND_VCC_SDA_SCL1.pin1, GND_A7_VCC.pin1
  N3: GND_A3_VCC.pin2, Nano.A3
  N4: GND_A3_VCC.pin3, GND_VCC_SDA_SCL.pin2, Vcc_GND_SDA_SCL.pin1, Nano.5V, GND_VCC_SDA_SCL1.pin2, GND_A7_VCC.pin3
  N5: GND_A2.pin2, Nano.A2
  N6: GND_VCC_SDA_SCL.pin3, Vcc_GND_SDA_SCL.pin3, Nano.A4, GND_VCC_SDA_SCL1.pin3
  N7: GND_VCC_SDA_SCL.pin4, Vcc_GND_SDA_SCL.pin4, Nano.A5, GND_VCC_SDA_SCL1.pin4
  N8: SDA_SCK_MOSI_MISO_GND_RST_3_3V.pin1, Nano.D10
  N9: SDA_SCK_MOSI_MISO_GND_RST_3_3V.pin2, Nano.D13/SCK
  N10: SDA_SCK_MOSI_MISO_GND_RST_3_3V.pin3, Nano.D11/MOSI
  N11: SDA_SCK_MOSI_MISO_GND_RST_3_3V.pin4, Nano.D12/MISO
  N12: SDA_SCK_MOSI_MISO_GND_RST_3_3V.pin7, Nano.D9
  N13: SDA_SCK_MOSI_MISO_GND_RST_3_3V.pin8, Nano.3V3
  N14: Nano.VIN, Switch.pin1
  N15: Nano.A7, GND_A7_VCC.pin2
  N16: GND_VIN_>5V.+, Switch.pin2

notes:
  Poti A3
  Analog D3
  Buzzer A2
  SDA
  SCK
  MOSI
  MISO
  RST
  VIN
  Geigerzaehler 2022 V3
  Buzzer
  Analog
  Poti
  Button
  Button A7
