# Fritzing sketch Geigerzähler 2020 V.2 (saved by Fritzing 0.9.3b)
circuit board: 6cm x 4cm
breadboards: 1

parts:
  D3_GND = female pin header, 2 pins [form="♀ (female)"]
  GND_A3_VCC = female pin header, 3 pins [form="♀ (female)"]
  GND_A7_VCC = female pin header, 3 pins [form="♀ (female)"]
  GND_A2 = female pin header, 2 pins [form="♀ (female)"]
  GND_VCC_SDA_SCL = female pin header, 4 pins [form="♀ (female)"]
  S1 = Pushbutton [package=THT]
  Vcc_GND_SDA_SCL = female pin header, 6 pins [form="♀ (female)"]
  SDA_SCK_MOSI_MISO_GND_RST_3_3V = female pin header, 8 pins [form="♀ (female)"]
  Nano = Arduino Nano (Rev3.0)
  GND_VIN = Battery block 9V
  VCC_D8_D7_LED_D5_D4_GND = female pin header, 7 pins [form="♀ (female)"]
  VCC_A0_A1_A6_GND = female pin header, 5 pins [form="♀ (female)"]
  VCC_D6_GND = female pin header, 3 pins [form="♀ (female)"]
  LM1117 = Voltage Regulator LM1117 [package=sot223]

nets:
  N1: D3_GND.pin1, Nano.D3
  N2: D3_GND.pin2, GND_A3_VCC.pin1, GND_A7_VCC.pin1, GND_A2.pin1, GND_VCC_SDA_SCL.pin1, Vcc_GND_SDA_SCL.pin2, SDA_SCK_MOSI_MISO_GND_RST_3_3V.pin6, Nano.GND, GND_VIN.-, VCC_D8_D7_LED_D5_D4_GND.pin1, VCC_A0_A1_A6_GND.pin5, VCC_D6_GND.pin3, LM1117.ADJ
  N3: GND_A3_VCC.pin2, Nano.A3
  N4: GND_A3_VCC.pin3, GND_A7_VCC.pin3, GND_VCC_SDA_SCL.pin2, Vcc_GND_SDA_SCL.pin1, Nano.5V, VCC_D8_D7_LED_D5_D4_GND.pin7, VCC_A0_A1_A6_GND.pin1
  N5: GND_A7_VCC.pin2, Nano.A7
  N6: GND_A2.pin2, Nano.A2
  N7: GND_VCC_SDA_SCL.pin3, Vcc_GND_SDA_SCL.pin3, Nano.A4
  N8: GND_VCC_SDA_SCL.pin4, Vcc_GND_SDA_SCL.pin4, Nano.A5
  N9: S1.leg0, Nano.VIN, LM1117.IN
  N10: S1.leg1, GND_VIN.+
  N11: SDA_SCK_MOSI_MISO_GND_RST_3_3V.pin1, Nano.D10
  N12: SDA_SCK_MOSI_MISO_GND_RST_3_3V.pin2, Nano.D13/SCK
  N13: SDA_SCK_MOSI_MISO_GND_RST_3_3V.pin3, Nano.D11/MOSI
  N14: SDA_SCK_MOSI_MISO_GND_RST_3_3V.pin4, Nano.D12/MISO
  N15: SDA_SCK_MOSI_MISO_GND_RST_3_3V.pin7, Nano.D9
  N16: SDA_SCK_MOSI_MISO_GND_RST_3_3V.pin8, Nano.3V3
  N17: Nano.D4, VCC_D8_D7_LED_D5_D4_GND.pin2
  N18: Nano.D5, VCC_D8_D7_LED_D5_D4_GND.pin3
  N19: Nano.D6, VCC_D8_D7_LED_D5_D4_GND.pin4, VCC_D6_GND.pin2
  N20: Nano.D7, VCC_D8_D7_LED_D5_D4_GND.pin5
  N21: Nano.D8, VCC_D8_D7_LED_D5_D4_GND.pin6
  N22: Nano.A6, VCC_A0_A1_A6_GND.pin4
  N23: Nano.A1, VCC_A0_A1_A6_GND.pin3
  N24: Nano.A0, VCC_A0_A1_A6_GND.pin2
  N25: VCC_D6_GND.pin1, LM1117.OUT

notes:
  Poti A3
  Joypad A7
  Analog D3
  Buzzer A2
  SDA
  SCK
  MOSI
  MISO
  RST
  LED D6
  VIN
