# Fritzing sketch Geigerzähler 2022 V.2_restore (saved by Fritzing 0.9.3b)
circuit board: 6cm x 4cm
breadboards: 1

parts:
  D3_GND = female pin header, 2 pins [form="♀ (female)"]
  GND_A3_VCC = female pin header, 3 pins [form="♀ (female)"]
  GND_A2 = female pin header, 2 pins [form="♀ (female)"]
  GND_VCC_SDA_SCL = female pin header, 4 pins [form="♀ (female)"]
  Vcc_GND_SDA_SCL = female pin header, 6 pins [form="♀ (female)"]
  SDA_SCK_MOSI_MISO_GND_RST_3_3V = female pin header, 8 pins [form="♀ (female)"]
  Nano = Arduino Nano (Rev3.0)
  GND_VIN_>5V = Battery block 9V
  LM1117 = Voltage Regulator LM1117 [package=sot223]
  SW1 = DIP Switch 4 Position [package=dipswitch-04]
  R1 = Resistor [tolerance=±5% resistance=220 package=THT]
  A+_A-_-_Vin_Gnd = female pin header, 5 pins [form="♀ (female)"]
  5V = Pad [width=1.2160224391878225 height=3.6339981193217974 connect=center]
  Pad7 = Pad [width=1.2160224391878225 height=3.6339981193217974 connect=center]  # not connected
  >5V = Pad [width=1.2160224391878225 height=3.6339981193217974 connect=center]
  Gnd_Vin_5V = female pin header, 2 pins [form="♀ (female)"]
  Gnd_Vin_5V_2 = female pin header, 2 pins [form="♀ (female)"]
  Switch = female pin header, 2 pins [form="♀ (female)"]
  Switch_2 = female pin header, 2 pins [form="♀ (female)"]

nets:
  N1: D3_GND.pin1, Nano.D3
  N2: D3_GND.pin2, GND_A3_VCC.pin1, GND_A2.pin1, GND_VCC_SDA_SCL.pin1, Vcc_GND_SDA_SCL.pin2, SDA_SCK_MOSI_MISO_GND_RST_3_3V.pin6, Nano.GND, GND_VIN_>5V.-, LM1117.ADJ, R1.Pin_1, A+_A-_-_Vin_Gnd.pin1, A+_A-_-_Vin_Gnd.pin4, Gnd_Vin_5V.pin2, Gnd_Vin_5V_2.pin2
  N3: GND_A3_VCC.pin2, Nano.A3
  N4: GND_A3_VCC.pin3, GND_VCC_SDA_SCL.pin2, Vcc_GND_SDA_SCL.pin1, Nano.5V, Switch_2.pin2
  N5: GND_A2.pin2, Nano.A2
  N6: GND_VCC_SDA_SCL.pin3, Vcc_GND_SDA_SCL.pin3, Nano.A4
  N7: GND_VCC_SDA_SCL.pin4, Vcc_GND_SDA_SCL.pin4, Nano.A5
  N8: SDA_SCK_MOSI_MISO_GND_RST_3_3V.pin1, Nano.D10
  N9: SDA_SCK_MOSI_MISO_GND_RST_3_3V.pin2, Nano.D13/SCK
  N10: SDA_SCK_MOSI_MISO_GND_RST_3_3V.pin3, Nano.D11/MOSI
  N11: SDA_SCK_MOSI_MISO_GND_RST_3_3V.pin4, Nano.D12/MISO
  N12: SDA_SCK_MOSI_MISO_GND_RST_3_3V.pin7, Nano.D9
  N13: SDA_SCK_MOSI_MISO_GND_RST_3_3V.pin8, Nano.3V3
  N14: Nano.D4, SW1.1
  N15: Nano.D5, SW1.2
  N16: Nano.D6, A+_A-_-_Vin_Gnd.pin5
  N17: Nano.D7, SW1.3
  N18: Nano.D8, SW1.4
  N19: Nano.VIN, LM1117.IN, Switch.pin1
  N20: GND_VIN_>5V.+, Switch.pin2
  N21: LM1117.OUT, A+_A-_-_Vin_Gnd.pin2, >5V.pad
  N22: SW1.5, SW1.6, SW1.7, SW1.8, R1.Pin_0
  N23: 5V.pad, Gnd_Vin_5V_2.pin1
  N24: Gnd_Vin_5V.pin1, Switch_2.pin1

notes:
  Poti A3
  Analog D3
  Buzzer A2
  SDA
  SCK
  MOSI
  MISO
  RST
  VIN
  Geigerzaehler 2022 V2
  Speaker D6
  Speaker Vin
  Platine Vin
