# Fritzing sketch Master_platine 6.0 (saved by Fritzing 0.9.3b)
circuit board: 10cm x 6.5cm
breadboards: 1

parts:
  GND_VCC_A0 = female pin header, 3 pins [form="♀ (female)"]
  GND_A1 = female pin header, 2 pins [form="♀ (female)"]
  GND_VCC_SDA_SCL = female pin header, 4 pins [form="♀ (female)"]
  M1 = Mega2560 R3 Pro ch340g
  SDA1_SCK_MOSI_MISO_-_GND_RST_3_3V = female pin header, 8 pins [form="♀ (female)"]
  GND_A2 = female pin header, 2 pins [form="♀ (female)"]
  GND_A4 = female pin header, 2 pins [form="♀ (female)"]
  CS_SCK_MoSi_MiSo_5V_GND = female pin header, 6 pins [form="♀ (female)"]
  Vcc_Gnd_SDA_SCL = female pin header, 6 pins [form="♀ (female)"]
  Power_plug1 = Power plug
  5V_A11_A9_A7_A5_Gnd = female pin header, 6 pins [form="♀ (female)"]
  D10_Vin_Gnd = female pin header, 3 pins [form="♀ (female)"]
  GND_max_5V-VIN = Battery
  R2 = Resistor [tolerance=±5% resistance=220 package=THT]
  R3 = Resistor [tolerance=±5% resistance=220 package=THT]
  R4 = Resistor [tolerance=±5% resistance=220 package=THT]
  RX3_TX3_GND = female pin header, 3 pins [form="♀ (female)"]
  CS_SCK_MoSi_MiSo_5V_GND1 = female pin header, 6 pins [form="♀ (female)"]
  5V_A14_GND = female pin header, 3 pins [form="♀ (female)"]
  SDA2_SCK_MOSI_MISO_-_GND_RST_3_3V1 = female pin header, 8 pins [form="♀ (female)"]
  Gnd_Vcc_SDA_SCL = female pin header, 6 pins [form="♀ (female)"]
  J1 = female pin header, 2 pins [form="♀ (female)"]
  GND_VCC_SW_DT_CLK = female pin header, 5 pins [form="♀ (female)"]
  GND_VIN_>5V = female pin header, 2 pins [form="♀ (female)"]

nets:
  GND: GND_VCC_A0.pin1, GND_A1.pin1, GND_VCC_SDA_SCL.pin1, M1.GND, SDA1_SCK_MOSI_MISO_-_GND_RST_3_3V.pin6, GND_A2.pin1, GND_A4.pin1, CS_SCK_MoSi_MiSo_5V_GND.pin1, Vcc_Gnd_SDA_SCL.pin5, Power_plug1.GND, 5V_A11_A9_A7_A5_Gnd.pin1, D10_Vin_Gnd.pin1, GND_max_5V-VIN.-, RX3_TX3_GND.pin3, CS_SCK_MoSi_MiSo_5V_GND1.pin1, 5V_A14_GND.pin3, SDA2_SCK_MOSI_MISO_-_GND_RST_3_3V1.pin6, Gnd_Vcc_SDA_SCL.pin6, GND_VCC_SW_DT_CLK.pin5, GND_VIN_>5V.pin1
  5V: GND_VCC_A0.pin2, GND_VCC_SDA_SCL.pin2, M1.VTG, M1.5V, CS_SCK_MoSi_MiSo_5V_GND.pin2, Vcc_Gnd_SDA_SCL.pin6, Power_plug1.VCC, 5V_A11_A9_A7_A5_Gnd.pin6, D10_Vin_Gnd.pin2, GND_max_5V-VIN.+, CS_SCK_MoSi_MiSo_5V_GND1.pin2, 5V_A14_GND.pin1, Gnd_Vcc_SDA_SCL.pin5, GND_VCC_SW_DT_CLK.pin4
  N1: GND_VCC_A0.pin3, M1.A0
  N2: GND_A1.pin2, M1.A1
  N3: GND_VCC_SDA_SCL.pin3, M1.20, Vcc_Gnd_SDA_SCL.pin4, Gnd_Vcc_SDA_SCL.pin4
  N4: GND_VCC_SDA_SCL.pin4, M1.21, Vcc_Gnd_SDA_SCL.pin3, Gnd_Vcc_SDA_SCL.pin3
  N5: M1.A5, 5V_A11_A9_A7_A5_Gnd.pin2
  N6: M1.A7, 5V_A11_A9_A7_A5_Gnd.pin3
  N7: M1.A9, 5V_A11_A9_A7_A5_Gnd.pin4
  N8: M1.A11, 5V_A11_A9_A7_A5_Gnd.pin5
  N9: M1.A14, 5V_A14_GND.pin2
  N10: M1.A4, R3.Pin_1
  N11: M1.A2, R4.Pin_1
  N12: M1.15, RX3_TX3_GND.pin1
  N13: M1.31, CS_SCK_MoSi_MiSo_5V_GND.pin6, CS_SCK_MoSi_MiSo_5V_GND1.pin6
  N14: M1.30, GND_VCC_SW_DT_CLK.pin2
  N15: M1.28, GND_VCC_SW_DT_CLK.pin1
  N16: M1.22, SDA2_SCK_MOSI_MISO_-_GND_RST_3_3V1.pin1
  N17: M1.18, SDA1_SCK_MOSI_MISO_-_GND_RST_3_3V.pin1
  N18: M1.16, SDA1_SCK_MOSI_MISO_-_GND_RST_3_3V.pin7, SDA2_SCK_MOSI_MISO_-_GND_RST_3_3V1.pin7
  N19: M1.14, RX3_TX3_GND.pin2
  N20: M1.10▀, D10_Vin_Gnd.pin3
  N21: M1.Vin, GND_VIN_>5V.pin2
  N22: M1.3V3, SDA1_SCK_MOSI_MISO_-_GND_RST_3_3V.pin8, SDA2_SCK_MOSI_MISO_-_GND_RST_3_3V1.pin8
  N23: M1.51/MOSI, SDA1_SCK_MOSI_MISO_-_GND_RST_3_3V.pin3, CS_SCK_MoSi_MiSo_5V_GND.pin4, CS_SCK_MoSi_MiSo_5V_GND1.pin4, SDA2_SCK_MOSI_MISO_-_GND_RST_3_3V1.pin3
  N24: M1.52/SCK, SDA1_SCK_MOSI_MISO_-_GND_RST_3_3V.pin2, CS_SCK_MoSi_MiSo_5V_GND.pin5, CS_SCK_MoSi_MiSo_5V_GND1.pin5, SDA2_SCK_MOSI_MISO_-_GND_RST_3_3V1.pin2
  N25: M1.50/MISO, SDA1_SCK_MOSI_MISO_-_GND_RST_3_3V.pin4, R2.Pin_1, SDA2_SCK_MOSI_MISO_-_GND_RST_3_3V1.pin4
  N26: SDA1_SCK_MOSI_MISO_-_GND_RST_3_3V.pin5, SDA2_SCK_MOSI_MISO_-_GND_RST_3_3V1.pin5
  N27: GND_A2.pin2, R4.Pin_0
  N28: GND_A4.pin2, R3.Pin_0
  N29: CS_SCK_MoSi_MiSo_5V_GND.pin3, R2.Pin_0, CS_SCK_MoSi_MiSo_5V_GND1.pin3
  N30: Vcc_Gnd_SDA_SCL.pin1, Gnd_Vcc_SDA_SCL.pin1, J1.pin1
  N31: Vcc_Gnd_SDA_SCL.pin2, Gnd_Vcc_SDA_SCL.pin2, J1.pin2

notes:
  Joypad A0
  Buzzer A1
  SDA1 D18
  RST D16
  CS D31
  LED 2 A4
  LED 1 A2
  POTI A14
  SDA2 D22
  SW Int X
  CLK 28
  DT 30

custom parts:
  Mega2560 R3 Pro ch340g: The Mega 2560 R3 Pro Mini :- Completely compatible with original Arduino Mega2560 Pin pitch: 0.1 inch Size: 5.42cm*3.68cm With Atmega16U2 chip as the USB to Serial converter 5V working voltage. Input Voltage:7-12V Analog Input Pins: 16 Digital I/O pins: 54 The Mega 2560 R3 Pro Mini has no datasheet and no info and I don't have one to compare, so I made this based on photos. Dec 2019 modified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
